// Logisim project circuit1a.circ as structural Verilog: 1 circuit, main circuit A
module A (
  input  C,
  input  B,
  input  A,
  output result
);

  wire AnotC_out, BnotC_out, CB_out, not_1_out, not_2_out, xor_1_out, xor_2_out;

  and CB (CB_out, C, B);
  not not_1 (not_1_out, C);
  not not_2 (not_2_out, C);
  xor xor_1 (xor_1_out, CB_out, A);
  and BnotC (BnotC_out, B, not_1_out);
  and AnotC (AnotC_out, A, not_2_out);
  xor xor_2 (xor_2_out, xor_1_out, BnotC_out);
  or or_1 (result, xor_2_out, AnotC_out);

  // Other names for the same wires on the sheet: inA = A; inB = B; inC = C
endmodule
