// Logisim project circuit1c.circ as structural Verilog: 1 circuit, main circuit main
module main (
  input  A,
  input  B,
  input  C,
  output result
);

  wire ABC_out, AnotBC_out, BC_out, notA_out, notAC_out, notACorAnotBC_out, notB_out, notBC_out, notC_out;

  not notA (notA_out, A);
  not notC (notC_out, C);
  not notB (notB_out, B);
  and notAC (notAC_out, notA_out, notC_out);
  and notBC (notBC_out, notB_out, notC_out);
  and BC (BC_out, B, C);
  buf AnotBC (AnotBC_out, notBC_out);  // AND_Gate
  and ABC (ABC_out, A, BC_out);
  or notACorAnotBC (notACorAnotBC_out, notAC_out, AnotBC_out);
  or fin (result, notACorAnotBC_out, ABC_out);

  // Other names for the same wires on the sheet: inA = A; inB = B; inC = C
endmodule
