// Logisim project my_adder.circ as structural Verilog: 5 circuits, main circuit main
module main (
  input  sub,
  input  [15:0] A,
  input  [15:0] B,
  output [15:0] result,
  output ovf
);

  wire fouradder_1_cout, fouradder_2_cout, fouradder_3_cout;
  wire [3:0] xorpass_1_valout, xorpass_2_valout, xorpass_3_valout, xorpass_4_valout;

  xorpass xorpass_1 (.valout(xorpass_1_valout), .val(B[3:0]), .sub(sub));
  xorpass xorpass_2 (.valout(xorpass_2_valout), .val(B[7:4]), .sub(sub));
  xorpass xorpass_3 (.valout(xorpass_3_valout), .val(B[11:8]), .sub(sub));
  xorpass xorpass_4 (.valout(xorpass_4_valout), .val(B[15:12]), .sub(sub));
  fouradder fouradder_1 (.Cin(sub), .A(A[3:0]), .B(xorpass_1_valout), .Sum(result[3:0]), .Cout(fouradder_1_cout));
  fouradder fouradder_2 (
    .Cin(fouradder_1_cout), .A(A[7:4]), .B(xorpass_2_valout), .Sum(result[7:4]), .Cout(fouradder_2_cout));
  fouradder fouradder_3 (
    .Cin(fouradder_2_cout), .A(A[11:8]), .B(xorpass_3_valout), .Sum(result[11:8]), .Cout(fouradder_3_cout));
  fouroverflow fouroverflow_1 (
    .Cin(fouradder_3_cout), .A(A[15:12]), .B(xorpass_4_valout), .Sum(result[15:12]), .ovf(ovf));
endmodule

module one (
  input  Cin,
  input  A,
  input  B,
  output Sum,
  output Cout
);

  wire and_1_out, and_2_out, xor_1_out;

  xor xor_1 (xor_1_out, A, B);
  xor xor_2 (Sum, Cin, xor_1_out);
  and and_1 (and_1_out, xor_1_out, Cin);
  and and_2 (and_2_out, A, B);
  or or_1 (Cout, and_1_out, and_2_out);

  // Other names for the same wires on the sheet: inA = A; inB = B; inCin = Cin
endmodule

module fouradder (
  input  Cin,
  input  [3:0] A,
  input  [3:0] B,
  output [3:0] Sum,
  output Cout
);

  wire one_1_cout, one_2_cout, one_3_cout;

  one one_1 (.Cin(Cin), .A(A[0]), .B(B[0]), .Sum(Sum[0]), .Cout(one_1_cout));
  one one_2 (.Cin(one_1_cout), .A(A[1]), .B(B[1]), .Sum(Sum[1]), .Cout(one_2_cout));
  one one_3 (.Cin(one_2_cout), .A(A[2]), .B(B[2]), .Sum(Sum[2]), .Cout(one_3_cout));
  one one_4 (.Cin(one_3_cout), .A(A[3]), .B(B[3]), .Sum(Sum[3]), .Cout(Cout));
endmodule

module fouroverflow (
  input  Cin,
  input  [3:0] A,
  input  [3:0] B,
  output [3:0] Sum,
  output ovf
);

  wire one_1_cout, one_2_cout, one_3_cout, one_4_cout;

  one one_1 (.Cin(Cin), .A(A[0]), .B(B[0]), .Sum(Sum[0]), .Cout(one_1_cout));
  one one_2 (.Cin(one_1_cout), .A(A[1]), .B(B[1]), .Sum(Sum[1]), .Cout(one_2_cout));
  one one_3 (.Cin(one_2_cout), .A(A[2]), .B(B[2]), .Sum(Sum[2]), .Cout(one_3_cout));
  one one_4 (.Cin(one_3_cout), .A(A[3]), .B(B[3]), .Sum(Sum[3]), .Cout(one_4_cout));
  xor xor_1 (ovf, one_3_cout, one_4_cout);
endmodule

module xorpass (
  input  sub,
  input  [3:0] val,
  output [3:0] valout
);

  xor xor_1 (valout[0], sub, val[0]);
  xor xor_2 (valout[1], sub, val[1]);
  xor xor_3 (valout[2], sub, val[2]);
  xor xor_4 (valout[3], sub, val[3]);
endmodule
