// Logisim project robot.circ as structural Verilog: 4 circuits, main circuit main
module main (
  input  in_1,
  input  in_speed,
  input  [1:0] in_leftright,
  output [1:0] out_position,
  output out_blocked
);

  wire clk, D0, D1, D2;

  D_Flip_Flop d_ff_1 (.D(D1), .clk(clk), .Q(out_position[1]), .reset(in_1));  // open: Qn, preset
  Clock clock_1 (.out(clk));
  D_Flip_Flop d_ff_2 (.D(D0), .clk(clk), .Q(out_position[0]), .reset(in_1));  // open: Qn, preset
  D2_converter d2_converter_1 (.Q1(out_position[1]), .Q0(out_position[0]), .input_leftright(in_leftright), .pos(D2));
  D0_converter d0_converter_1 (
    .Q2(out_blocked), .Q1(out_position[1]), .Q0(out_position[0]), .input_speed(in_speed),
    .input_leftright(in_leftright), .pos(D0));
  D1_converter d1_converter_1 (
    .Q2(out_blocked), .Q1(out_position[1]), .Q0(out_position[0]), .input_speed(in_speed),
    .input_leftright(in_leftright), .pos(D1));
  D_Flip_Flop d_ff_3 (.D(D2), .clk(clk), .Q(out_blocked), .reset(in_1));  // open: Qn, preset

  // Other names for the same wires on the sheet: inleftright[1:0] = in_leftright; Q0 = out_position[0];
  //   Q1 = out_position[1]; Q2 = out_blocked; reset = in_1; Speed = in_speed
endmodule

module D0_converter (
  input  Q2,
  input  Q1,
  input  Q0,
  input  input_speed,
  input  [1:0] input_leftright,
  output pos
);

  wire and_1_out, and_2_out, and_3_out, and_4_out, and_5_out, and_6_out, not_1_out, not_2_out, not_3_out,
       not_4_out, not_5_out, not_6_out, not_7_out, not_8_out, not_9_out, not_10_out, not_11_out, not_12_out,
       not_13_out;

  not not_1 (not_1_out, Q1);
  not not_2 (not_2_out, Q0);
  not not_3 (not_3_out, input_speed);
  not not_4 (not_4_out, input_leftright[0]);
  not not_5 (not_5_out, Q0);
  not not_6 (not_6_out, input_speed);
  not not_7 (not_7_out, input_leftright[1]);
  not not_8 (not_8_out, input_leftright[1]);
  not not_9 (not_9_out, Q1);
  not not_10 (not_10_out, input_leftright[0]);
  not not_11 (not_11_out, input_leftright[0]);
  not not_12 (not_12_out, input_leftright[0]);
  not not_13 (not_13_out, input_leftright[1]);
  and and_1 (and_1_out, not_1_out, not_2_out, not_3_out, input_leftright[1], not_4_out);
  and and_2 (and_2_out, Q1, not_5_out, not_6_out, not_7_out, input_leftright[0]);
  and and_3 (and_3_out, Q1, Q0, input_speed, not_8_out, input_leftright[0]);
  and and_4 (and_4_out, not_9_out, Q0, input_speed, input_leftright[1], not_10_out);
  and and_5 (and_5_out, Q1, not_11_out, input_leftright[1]);
  and and_6 (and_6_out, not_12_out, Q0, not_13_out);
  or or_1 (pos, and_1_out, and_2_out, and_3_out, and_4_out, and_5_out, and_6_out);

  // Other names for the same wires on the sheet: A = Q2; B = Q1; C = Q0; D = input_speed; F = input_leftright[0];
  //   E = input_leftright[1]
endmodule

module D1_converter (
  input  Q2,
  input  Q1,
  input  Q0,
  input  input_speed,
  input  [1:0] input_leftright,
  output pos
);

  wire and_1_out, and_2_out, and_3_out, and_4_out, not_1_out, not_2_out, not_3_out, not_4_out, not_5_out,
       not_6_out, not_7_out;

  not not_1 (not_1_out, Q1);
  not not_2 (not_2_out, Q0);
  not not_3 (not_3_out, input_leftright[0]);
  not not_4 (not_4_out, input_leftright[0]);
  not not_5 (not_5_out, input_speed);
  not not_6 (not_6_out, input_leftright[1]);
  not not_7 (not_7_out, input_leftright[0]);
  and and_1 (and_1_out, not_1_out, not_2_out, input_speed, input_leftright[1], not_3_out);
  and and_2 (and_2_out, Q1, not_4_out);
  and and_3 (and_3_out, Q1, Q0, not_5_out, not_6_out, input_leftright[0]);
  and and_4 (and_4_out, ~Q1, Q0, input_leftright[1], not_7_out);  // AND_Gate
  or or_1 (pos, and_1_out, and_2_out, and_3_out, and_4_out);

  // Other names for the same wires on the sheet: A = Q2; B = Q1; C = Q0; D = input_speed; F = input_leftright[0];
  //   E = input_leftright[1]
endmodule

module D2_converter (
  input  Q1,
  input  Q0,
  input  [1:0] input_leftright,
  output pos
);

  wire and_1_out, and_2_out, not_1_out, not_2_out, not_3_out, not_4_out;

  not not_1 (not_1_out, input_leftright[0]);
  not not_2 (not_2_out, Q1);
  not not_3 (not_3_out, Q0);
  not not_4 (not_4_out, input_leftright[1]);
  and and_1 (and_1_out, Q1, Q0, input_leftright[1], not_1_out);
  and and_2 (and_2_out, not_2_out, not_3_out, not_4_out, input_leftright[0]);
  or or_1 (pos, and_1_out, and_2_out);

  // Other names for the same wires on the sheet: B = Q1; C = Q0; F = input_leftright[0]; E = input_leftright[1]
endmodule
