// Logisim project cpu.circ as structural Verilog: 17 circuits, main circuit main
module main (
  input  reset
);

  wire clktun, kbwe, memory_latch_1_oe_latched, memory_latch_1_we_latched, not_1_out, scrnwe, writemem,
       writeout;
  wire [2:0] rd, rs, rt, shift, wport;
  wire [3:0] opcode;
  wire [5:0] instruct_decod_1_immed;
  wire [6:0] bit_extender_1_out, keyboard_1_data;
  wire [11:0] instruct_decod_1_address;
  wire [15:0] addedpc, addylonger, extended_outkey, findata, immed, instruction,
       memory_latch_1_address_latched, memory_latch_1_data_in_latched, outputdata, pc1, pcbeq, pcblt, ramout,
       valofrs, valofrt;

  Clock clk (.out(clktun));
  // Probe on rs
  Bit_Extender #(.in_width(16), .out_width(7)) bit_extender_1 (.in(valofrs), .out(bit_extender_1_out));
  // Probe on opcode
  TTY #(.rows(13), .cols(80)) tty_1 (.data(bit_extender_1_out), .clk(clktun), .we(scrnwe), .clr(reset));
  Keyboard keyboard_1 (.clk(clktun), .re(kbwe), .clr(reset), .data(keyboard_1_data));  // open: avail
  instruct_decod instruct_decod_1 (
    .insturct(instruction), .op(opcode), .rs(rs), .rt(rt), .rd(rd), .shamt(shift),
    .immed(instruct_decod_1_immed), .address(instruct_decod_1_address));
  control control_1 (.opcode(opcode), .we(writeout), .wm(writemem), .scrnwe(scrnwe), .kbwe(kbwe));
  // Probe on rs
  assign addylonger = {{4{1'b0}}, instruct_decod_1_address};  // Bit_Extender bit_extender_2
  assign immed = {{10{instruct_decod_1_immed[5]}}, instruct_decod_1_immed};  // Bit_Extender bit_extender_3
  // Probe on instruct_decod_1_address
  assign extended_outkey = {{9{1'b0}}, keyboard_1_data};  // Bit_Extender bit_extender_4
  // Probe on valofrs
  RegisterFile registerfile_1 (
    .res(reset), .clk(clktun), .datain(findata), .read01(rs), .RegEnable(writeout), .writereg(wport),
    .read02(rt), .dataout1(valofrs), .dataout2(valofrt));
  // Probe on immed
  // Probe on immed
  PC pc_1 (
    .clk(clktun), .rst(reset), .beqzpc(pcbeq), .bltpc(pcblt), .valofrs(valofrs), .opcode(opcode),
    .address(addylonger), .addedpc(addedpc), .currpc(pc1));
  beqz beqz_1 (.immed(immed), .valofrs(valofrs), .currpc(addedpc), .pcbeq(pcbeq));
  blt blt_1 (.currpc(addedpc), .valofrs(valofrs), .valofrt(valofrt), .immed(immed), .pcblt(pcblt));
  ALU alu_1 (
    .dataIn01(valofrs), .dataIn02(valofrt), .opType(opcode), .shift(shift), .immed(immed),
    .address(addylonger), .out_7(outputdata));
  not not_1 (not_1_out, clktun);
  // Probe on wport
  Multiplexer #(.select(4), .width(3), .enable("false")) multiplexer_1 (
    .in0(rd), .in1(rd), .in2(rt), .in3(rd), .in4(rd), .in5(rd), .in6(rd), .in7(rt), .in8(3'b000),
    .in9(3'b000), .in10(3'b000), .in11(3'b000), .in12(3'b000), .in13(3'b111), .in14(rd), .in15(3'b000),
    .out(wport), .sel(opcode));
  // Probe on opcode
  RAM #(.addrWidth(16), .dataWidth(16), .trigger("high"), .databus("bibus")) ram_1 (
    .addr(memory_latch_1_address_latched), .we(memory_latch_1_we_latched), .oe(memory_latch_1_oe_latched),
    .din(memory_latch_1_data_in_latched), .dout(ramout));
  memory_latch memory_latch_1 (
    .address(outputdata), .WE(writemem), .clk(not_1_out), .data_in(valofrt),
    .address_latched(memory_latch_1_address_latched), .WE_latched(memory_latch_1_we_latched),
    .OE_latched(memory_latch_1_oe_latched), .data_in_latched(memory_latch_1_data_in_latched));
  ROM #(.addrWidth(16), .dataWidth(16)) rom_1 (.addr(pc1), .data(instruction));
  // Probe on outputdata
  Multiplexer #(.select(4), .width(16), .enable("false")) multiplexer_2 (
    .in0(outputdata), .in1(outputdata), .in2(outputdata), .in3(outputdata), .in4(outputdata),
    .in5(outputdata), .in6(outputdata), .in7(ramout), .in8({16{1'b0}}), .in9({16{1'b0}}), .in10({16{1'b0}}),
    .in11({16{1'b0}}), .in12({16{1'b0}}), .in13(addedpc), .in14(extended_outkey), .in15({16{1'b0}}),
    .out(findata), .sel(opcode));
  // Probe on findata
  // Probe on ramout
  // Probe on instruction

  // Other names for the same wires on the sheet: resettun = reset

  // Notes on the sheet:
  //   what does instrucct decod do and how does it worjk?
  //   explain alu and reg file data path 
  //   is it val of rd or just rd?
  //   what is reg file ?
  //   what does PC do and how does it work?
  //   contents of rom_1 (hex, n*v repeats v):
  //   204b 208c 20cc 210d 2141 a446 2142 a4c6 2143 a506 2197 903f 219e 903f 219f 903f 207f 2144 a282 2198
  //   903f 2145 2041 9212 2146 2040 9202 2199 203f 2157 b021 219a 903f 2148 d025 214a 903f 2242 2149 ce00
  //   219b 903f 219c 903f
endmodule

module RegisterFile (
  input  res,
  input  clk,
  input  [15:0] datain,
  input  [2:0] read01,
  input  RegEnable,
  input  [2:0] writereg,
  input  [2:0] read02,
  output [15:0] dataout1,
  output [15:0] dataout2
);

  wire r10, r11, r12, r13, r14, r15, r16, r17, r20, r21, r22, r23, r24, r25, r26, r27, we1, we2, we3, we4,
       we5, we6, we7;
  wire [15:0] r1, r2, r3, r4, r5, r6, r7;

  Decoder #(.select(3)) decoder_1 (
    .out1(we1), .out2(we2), .out3(we3), .out4(we4), .out5(we5), .out6(we6), .out7(we7), .sel(writereg),
    .en(RegEnable));  // open: out0
  register16bit register16bit_1 (.D(datain), .clkin(clk), .we(we7), .set(res), .Q(r7));
  register16bit register16bit_2 (.D(datain), .clkin(clk), .we(we6), .set(res), .Q(r6));
  register16bit register16bit_3 (.D(datain), .clkin(clk), .we(we5), .set(res), .Q(r5));
  register16bit register16bit_4 (.D(datain), .clkin(clk), .we(we4), .set(res), .Q(r4));
  register16bit register16bit_5 (.D(datain), .clkin(clk), .we(we3), .set(res), .Q(r3));
  register16bit register16bit_6 (.D(datain), .clkin(clk), .we(we2), .set(res), .Q(r2));
  register16bit register16bit_7 (.D(datain), .clkin(clk), .we(we1), .set(res), .Q(r1));
  assign dataout2 = r27 ? r7 : 16'bz;  // Controlled_Buffer controlled_buffer_1
  assign dataout2 = r26 ? r6 : 16'bz;  // Controlled_Buffer controlled_buffer_2
  assign dataout2 = r25 ? r5 : 16'bz;  // Controlled_Buffer controlled_buffer_3
  assign dataout2 = r24 ? r4 : 16'bz;  // Controlled_Buffer controlled_buffer_4
  assign dataout2 = r23 ? r3 : 16'bz;  // Controlled_Buffer controlled_buffer_5
  assign dataout2 = r22 ? r2 : 16'bz;  // Controlled_Buffer controlled_buffer_6
  assign dataout2 = r21 ? r1 : 16'bz;  // Controlled_Buffer controlled_buffer_7
  assign dataout2 = r20 ? {16{1'b0}} : 16'bz;  // Controlled_Buffer controlled_buffer_8
  assign dataout1 = r17 ? r7 : 16'bz;  // Controlled_Buffer controlled_buffer_9
  assign dataout1 = r16 ? r6 : 16'bz;  // Controlled_Buffer controlled_buffer_10
  assign dataout1 = r15 ? r5 : 16'bz;  // Controlled_Buffer controlled_buffer_11
  assign dataout1 = r14 ? r4 : 16'bz;  // Controlled_Buffer controlled_buffer_12
  assign dataout1 = r13 ? r3 : 16'bz;  // Controlled_Buffer controlled_buffer_13
  assign dataout1 = r12 ? r2 : 16'bz;  // Controlled_Buffer controlled_buffer_14
  assign dataout1 = r11 ? r1 : 16'bz;  // Controlled_Buffer controlled_buffer_15
  assign dataout1 = r10 ? {16{1'b0}} : 16'bz;  // Controlled_Buffer controlled_buffer_16
  // Probe on nothing
  Decoder #(.select(3)) decoder_2 (
    .out0(r10), .out1(r11), .out2(r12), .out3(r13), .out4(r14), .out5(r15), .out6(r16), .out7(r17),
    .sel(read01));  // open: en
  Decoder #(.select(3)) decoder_3 (
    .out0(r20), .out1(r21), .out2(r22), .out3(r23), .out4(r24), .out5(r25), .out6(r26), .out7(r27),
    .sel(read02));  // open: en
  // Probe on r7
  // Probe on r6
  // Probe on r5
  // Probe on r4
  // Probe on r3
  // Probe on r2
  // Probe on r1
  // Probe on {16{1'b0}}

  // Other names for the same wires on the sheet: clktun = clk; rst = res
endmodule

module register16bit (
  input  [15:0] D,
  input  clkin,
  input  we,
  input  set,
  output [15:0] Q
);

  wire clk;

  and and_1 (clk, clkin, we);
  D_Flip_Flop d_ff_1 (.D(D[0]), .clk(clk), .Q(Q[0]));  // open: Qn, preset, reset
  D_Flip_Flop d_ff_2 (.D(D[1]), .clk(clk), .Q(Q[1]));  // open: Qn, preset, reset
  D_Flip_Flop d_ff_3 (.D(D[2]), .clk(clk), .Q(Q[2]), .reset(set));  // open: Qn, preset
  D_Flip_Flop d_ff_4 (.D(D[3]), .clk(clk), .Q(Q[3]), .reset(set));  // open: Qn, preset
  D_Flip_Flop d_ff_5 (.D(D[4]), .clk(clk), .Q(Q[4]), .reset(set));  // open: Qn, preset
  D_Flip_Flop d_ff_6 (.D(D[5]), .clk(clk), .Q(Q[5]), .reset(set));  // open: Qn, preset
  D_Flip_Flop d_ff_7 (.D(D[6]), .clk(clk), .Q(Q[6]), .reset(set));  // open: Qn, preset
  D_Flip_Flop d_ff_8 (.D(D[7]), .clk(clk), .Q(Q[7]), .reset(set));  // open: Qn, preset
  D_Flip_Flop d_ff_9 (.D(D[8]), .clk(clk), .Q(Q[8]), .reset(set));  // open: Qn, preset
  D_Flip_Flop d_ff_10 (.D(D[9]), .clk(clk), .Q(Q[9]), .reset(set));  // open: Qn, preset
  D_Flip_Flop d_ff_11 (.D(D[10]), .clk(clk), .Q(Q[10]), .reset(set));  // open: Qn, preset
  D_Flip_Flop d_ff_12 (.D(D[11]), .clk(clk), .Q(Q[11]), .reset(set));  // open: Qn, preset
  D_Flip_Flop d_ff_13 (.D(D[12]), .clk(clk), .Q(Q[12]), .reset(set));  // open: Qn, preset
  D_Flip_Flop d_ff_14 (.D(D[13]), .clk(clk), .Q(Q[13]), .reset(set));  // open: Qn, preset
  D_Flip_Flop d_ff_15 (.D(D[14]), .clk(clk), .Q(Q[14]), .reset(set));  // open: Qn, preset
  D_Flip_Flop d_ff_16 (.D(D[15]), .clk(clk), .Q(Q[15]), .reset(set));  // open: Qn, preset

  // Other names for the same wires on the sheet: reset = set
endmodule

module ALU (
  input  [15:0] dataIn01,
  input  [15:0] dataIn02,
  input  [3:0] opType,
  input  [2:0] shift,
  input  [15:0] immed,
  input  [15:0] address,
  output [15:0] out_7
);

  wire [15:0] add, immedout, inNot, inXOR, leftshift, rightshift, sub;

  assign inNot = ~dataIn01;  // NOT_Gate not_1, 16 bits wide
  assign inXOR = dataIn01 ^ dataIn02;  // XOR_Gate xor_1, 16 bits wide
  adder16bit adder16bit_1 (.A(dataIn01), .B(dataIn02), .res(add));  // open: Cin, ovf
  adder16bit adder16bit_2 (.Cin(1'b1), .A(dataIn01), .B(dataIn02), .res(sub));  // open: ovf
  left_shifter left_shifter_1 (.in_1(dataIn01), .in_2(shift), .out_3(leftshift));
  right_shifter right_shifter_1 (.srlin(dataIn01), .shift(shift), .rightout(rightshift));
  adder16bit adder16bit_3 (.A(dataIn01), .B(immed), .res(immedout));  // open: Cin, ovf
  Multiplexer #(.select(4), .width(16), .enable("false")) multiplexer_1 (
    .in0(add), .in1(sub), .in2(immedout), .in3(inNot), .in4(inXOR), .in5(leftshift), .in6(rightshift),
    .in7(immedout), .in8(immedout), .in13(address), .out(out_7), .sel(opType));  // open: in9, in10, in11, in12, in14, in15

  // Other names for the same wires on the sheet: addytun[15:0] = address
endmodule

module adder16bit (
  input  Cin,
  input  [15:0] A,
  input  [15:0] B,
  output [15:0] res,
  output ovf
);

  wire fouradder_1_cout, fouradder_2_cout, fouradder_3_cout;
  wire [3:0] xorpass_1_valout, xorpass_2_valout, xorpass_3_valout, xorpass_4_valout;

  xorpass xorpass_1 (.valout(xorpass_1_valout), .val(B[3:0]), .sub(Cin));
  xorpass xorpass_2 (.valout(xorpass_2_valout), .val(B[7:4]), .sub(Cin));
  xorpass xorpass_3 (.valout(xorpass_3_valout), .val(B[11:8]), .sub(Cin));
  xorpass xorpass_4 (.valout(xorpass_4_valout), .val(B[15:12]), .sub(Cin));
  fouradder fouradder_1 (.Cin(Cin), .A(A[3:0]), .B(xorpass_1_valout), .Sum(res[3:0]), .Cout(fouradder_1_cout));
  fouradder fouradder_2 (
    .Cin(fouradder_1_cout), .A(A[7:4]), .B(xorpass_2_valout), .Sum(res[7:4]), .Cout(fouradder_2_cout));
  fouradder fouradder_3 (
    .Cin(fouradder_2_cout), .A(A[11:8]), .B(xorpass_3_valout), .Sum(res[11:8]), .Cout(fouradder_3_cout));
  fouroverflow fouroverflow_1 (.Cin(fouradder_3_cout), .A(A[15:12]), .B(xorpass_4_valout), .Sum(res[15:12]), .ovf(ovf));
endmodule

module Fulladder (
  input  Cin,
  input  A,
  input  B,
  output Sum,
  output Cout
);

  wire and_1_out, and_2_out, xor_1_out;

  xor xor_1 (xor_1_out, A, B);
  xor xor_2 (Sum, Cin, xor_1_out);
  and and_1 (and_1_out, xor_1_out, Cin);
  and and_2 (and_2_out, A, B);
  or or_1 (Cout, and_1_out, and_2_out);

  // Other names for the same wires on the sheet: inA = A; inB = B; inCin = Cin
endmodule

module fouradder (
  input  Cin,
  input  [3:0] A,
  input  [3:0] B,
  output [3:0] Sum,
  output Cout
);

  wire fulladder_1_cout, fulladder_2_cout, fulladder_3_cout;

  Fulladder fulladder_1 (.Cin(Cin), .A(A[0]), .B(B[0]), .Sum(Sum[0]), .Cout(fulladder_1_cout));
  Fulladder fulladder_2 (.Cin(fulladder_1_cout), .A(A[1]), .B(B[1]), .Sum(Sum[1]), .Cout(fulladder_2_cout));
  Fulladder fulladder_3 (.Cin(fulladder_2_cout), .A(A[2]), .B(B[2]), .Sum(Sum[2]), .Cout(fulladder_3_cout));
  Fulladder fulladder_4 (.Cin(fulladder_3_cout), .A(A[3]), .B(B[3]), .Sum(Sum[3]), .Cout(Cout));
endmodule

module fouroverflow (
  input  Cin,
  input  [3:0] A,
  input  [3:0] B,
  output [3:0] Sum,
  output ovf
);

  wire fulladder_1_cout, fulladder_2_cout, fulladder_3_cout, fulladder_4_cout;

  Fulladder fulladder_1 (.Cin(Cin), .A(A[0]), .B(B[0]), .Sum(Sum[0]), .Cout(fulladder_1_cout));
  Fulladder fulladder_2 (.Cin(fulladder_1_cout), .A(A[1]), .B(B[1]), .Sum(Sum[1]), .Cout(fulladder_2_cout));
  Fulladder fulladder_3 (.Cin(fulladder_2_cout), .A(A[2]), .B(B[2]), .Sum(Sum[2]), .Cout(fulladder_3_cout));
  Fulladder fulladder_4 (.Cin(fulladder_3_cout), .A(A[3]), .B(B[3]), .Sum(Sum[3]), .Cout(fulladder_4_cout));
  xor xor_1 (ovf, fulladder_3_cout, fulladder_4_cout);
endmodule

module xorpass (
  input  sub,
  input  [3:0] val,
  output [3:0] valout
);

  xor xor_1 (valout[0], sub, val[0]);
  xor xor_2 (valout[1], sub, val[1]);
  xor xor_3 (valout[2], sub, val[2]);
  xor xor_4 (valout[3], sub, val[3]);
endmodule

module left_shifter (
  input  [15:0] in_1,
  input  [2:0] in_2,
  output [15:0] out_3
);

  wire [15:2] b1;
  wire [15:4] b2;
  wire [15:12] multiplexer_2_out;
  wire [15:14] multiplexer_1_out;

  Multiplexer #(.width(16), .enable("false")) multiplexer_1 (
    .in0(in_1), .in1({in_1[14:0], 1'b0}), .out({multiplexer_1_out, b1}), .sel(in_2[0]));
  Multiplexer #(.width(16), .enable("false")) multiplexer_2 (
    .in0({multiplexer_1_out, b1}), .in1({b1, 2'b00}), .out({multiplexer_2_out, b2}), .sel(in_2[1]));
  Multiplexer #(.width(16), .enable("false")) multiplexer_3 (
    .in0({multiplexer_2_out, b2}), .in1({b2, 4'b0000}), .out(out_3), .sel(in_2[2]));

  // Other names for the same wires on the sheet: s0 = in_2[0]; s1 = in_2[1]; s2 = in_2[2]; b0[15:1] = in_1[14:0];
  //   intun[15:0] = in_1
endmodule

module right_shifter (
  input  [15:0] srlin,
  input  [2:0] shift,
  output [15:0] rightout
);

  wire [1:0] multiplexer_1_out;
  wire [3:0] multiplexer_2_out;
  wire [11:0] b2;
  wire [13:0] b1;

  Multiplexer #(.width(16), .enable("false")) multiplexer_1 (
    .in0(srlin), .in1({1'b0, srlin[15:1]}), .out({b1, multiplexer_1_out}), .sel(shift[0]));
  Multiplexer #(.width(16), .enable("false")) multiplexer_2 (
    .in0({b1, multiplexer_1_out}), .in1({2'b00, b1}), .out({b2, multiplexer_2_out}), .sel(shift[1]));
  Multiplexer #(.width(16), .enable("false")) multiplexer_3 (
    .in0({b2, multiplexer_2_out}), .in1({4'b0000, b2}), .out(rightout), .sel(shift[2]));

  // Other names for the same wires on the sheet: intun[15:0] = srlin; b0[14:0] = srlin[15:1]; s0 = shift[0];
  //   s1 = shift[1]; s2 = shift[2]
endmodule

module instruct_decod (
  input  [15:0] insturct,
  output [3:0] op,
  output [2:0] rs,
  output [2:0] rt,
  output [2:0] rd,
  output [2:0] shamt,
  output [5:0] immed,
  output [11:0] address
);


  assign address = insturct[11:0];
  assign immed = insturct[5:0];
  assign op = insturct[15:12];
  assign rd = insturct[5:3];
  assign rs = insturct[11:9];
  assign rt = insturct[8:6];
  assign shamt = insturct[2:0];

  // Other names for the same wires on the sheet: opcode[3:0] = insturct[15:12]
endmodule

module PC (
  input  clk,
  input  rst,
  input  [15:0] beqzpc,
  input  [15:0] bltpc,
  input  [15:0] valofrs,
  input  [3:0] opcode,
  input  [15:0] address,
  output [15:0] addedpc,
  output [15:0] currpc
);

  wire not_1_out;
  wire [15:0] pcchooser;

  not not_1 (not_1_out, clk);
  register16bit register16bit_1 (.D(pcchooser), .clkin(not_1_out), .we(1'b1), .set(rst), .Q(currpc));
  Multiplexer #(.select(4), .width(16), .enable("false")) multiplexer_1 (
    .in0(addedpc), .in1(addedpc), .in2(addedpc), .in3(addedpc), .in4(addedpc), .in5(addedpc), .in6(addedpc),
    .in7(addedpc), .in8(addedpc), .in9(beqzpc), .in10(bltpc), .in11(address), .in12(valofrs), .in13(address),
    .in14(addedpc), .in15(addedpc), .out(pcchooser), .sel(opcode));
  adder16bit adder16bit_1 (.A(currpc), .B(16'h1), .res(addedpc));  // open: Cin, ovf
  // Probe on pcchooser

  // Other names for the same wires on the sheet: addPC[15:0] = addedpc

  // Notes on the sheet:
  //   IF I MUX BETWEEN WHAT IS BEING ADDED RIGHT HERE THEN I CAN DETERMINE WHAT IS BEING ADDED INTOTAL 
endmodule

module memory_latch (
  input  [15:0] address,
  input  WE,
  input  clk,
  input  [15:0] data_in,
  output [15:0] address_latched,
  output WE_latched,
  output OE_latched,
  output [15:0] data_in_latched
);

  wire DMwe_latch_q;
  wire [15:0] addr_latch_q;

  Register #(.width(16), .trigger("falling")) addr_latch (
    .D(address), .en(WE), .clk(clk), .Q(addr_latch_q));  // open: clr
  D_Flip_Flop #(.trigger("falling")) DMwe_latch (.D(WE), .clk(clk), .Q(DMwe_latch_q));  // open: Qn, preset, reset
  Register #(.width(16), .trigger("falling")) data_to_be_written (
    .D(data_in), .en(WE), .clk(clk), .Q(data_in_latched));  // open: clr
  Multiplexer #(.width(16), .enable("false")) multiplexer_1 (
    .in0(address), .in1(addr_latch_q), .out(address_latched), .sel(DMwe_latch_q));
  and and_1 (WE_latched, clk, DMwe_latch_q);
  not not_1 (OE_latched, WE_latched);
endmodule

module control (
  input  [3:0] opcode,
  output we,
  output wm,
  output scrnwe,
  output kbwe
);

  wire and_1_out, and_2_out, not_1_out, not_2_out, not_3_out, not_4_out, not_5_out, not_6_out, not_7_out;

  not not_1 (not_1_out, opcode[1]);
  not not_2 (not_2_out, opcode[0]);
  not not_3 (not_3_out, opcode[3]);
  and and_1 (and_1_out, opcode[3], opcode[2], not_1_out, opcode[0]);
  and and_2 (and_2_out, opcode[3], opcode[2], opcode[1], not_2_out);
  not not_4 (not_4_out, opcode[2]);
  not not_5 (not_5_out, opcode[1]);
  not not_6 (not_6_out, opcode[0]);
  not not_7 (not_7_out, opcode[0]);
  and and_3 (wm, opcode[3], not_4_out, not_5_out, not_6_out);
  and and_4 (scrnwe, opcode[3], opcode[2], opcode[1], opcode[0]);
  and and_5 (kbwe, opcode[3], opcode[2], opcode[1], not_7_out);
  or or_1 (we, not_3_out, and_1_out, and_2_out);

  // Other names for the same wires on the sheet: d = opcode[0]; c = opcode[1]; b = opcode[2]; a = opcode[3]
endmodule

module beqz (
  input  [15:0] immed,
  input  [15:0] valofrs,
  input  [15:0] currpc,
  output [15:0] pcbeq
);

  wire not_1_out, or_1_out;
  wire [15:0] multiplexer_1_out;

  or or_1 (or_1_out, valofrs[0], valofrs[1], valofrs[2], valofrs[3], valofrs[4], valofrs[5], valofrs[6], valofrs[7], valofrs[8], valofrs[9], valofrs[10], valofrs[11], valofrs[12], valofrs[13], valofrs[14], valofrs[15]);
  Multiplexer #(.width(16), .enable("false")) multiplexer_1 (
    .in0({16{1'b0}}), .in1(immed), .out(multiplexer_1_out), .sel(not_1_out));
  not not_1 (not_1_out, or_1_out);
  adder16bit adder16bit_1 (.A(currpc), .B(multiplexer_1_out), .res(pcbeq));  // open: Cin, ovf
endmodule

module blt (
  input  [15:0] currpc,
  input  [15:0] valofrs,
  input  [15:0] valofrt,
  input  [15:0] immed,
  output [15:0] pcblt
);

  wire [15:0] adder16bit_1_res, multiplexer_1_out;

  adder16bit adder16bit_1 (.Cin(1'b1), .A(valofrs), .B(valofrt), .res(adder16bit_1_res));  // open: ovf
  Multiplexer #(.width(16), .enable("false")) multiplexer_1 (
    .in0({16{1'b0}}), .in1(immed), .out(multiplexer_1_out), .sel(adder16bit_1_res[15]));
  adder16bit adder16bit_2 (.A(multiplexer_1_out), .B(currpc), .res(pcblt));  // open: Cin, ovf
endmodule
