// Logisim project resgisterfile.circ as structural Verilog
module regfile (
  input  res,
  input  clk,
  input  [2:0] read01,
  input  [15:0] datain,
  input  [2:0] read02,
  input  [2:0] writereg,
  output [15:0] dataout1,
  output [15:0] dataout2
);

  wire decoder_1_out1, decoder_1_out2, decoder_1_out3, decoder_1_out4, decoder_1_out5, decoder_1_out6,
       decoder_1_out7, r10, r11, r12, r13, r14, r15, r16, r17, r20, r21, r22, r23, r24, r25, r26, r27;
  wire [15:0] register16bit_1_q, register16bit_2_q, register16bit_3_q, register16bit_4_q, register16bit_5_q,
       register16bit_6_q, register16bit_7_q, register16bit_8_q;

  Decoder #(.select(3)) decoder_1 (
    .out1(decoder_1_out1), .out2(decoder_1_out2), .out3(decoder_1_out3), .out4(decoder_1_out4),
    .out5(decoder_1_out5), .out6(decoder_1_out6), .out7(decoder_1_out7), .sel(writereg));  // open: out0, en
  register16bit register16bit_1 (.D(datain), .clkin(clk), .we(decoder_1_out7), .set(res), .Q(register16bit_1_q));
  register16bit register16bit_2 (.D(datain), .clkin(clk), .we(decoder_1_out6), .set(res), .Q(register16bit_2_q));
  register16bit register16bit_3 (.D(datain), .clkin(clk), .we(decoder_1_out5), .set(res), .Q(register16bit_3_q));
  register16bit register16bit_4 (.D(datain), .clkin(clk), .we(decoder_1_out4), .set(res), .Q(register16bit_4_q));
  register16bit register16bit_5 (.D(datain), .clkin(clk), .we(decoder_1_out3), .set(res), .Q(register16bit_5_q));
  register16bit register16bit_6 (.D(datain), .clkin(clk), .we(decoder_1_out2), .set(res), .Q(register16bit_6_q));
  register16bit register16bit_7 (.D(datain), .clkin(clk), .we(decoder_1_out1), .set(res), .Q(register16bit_7_q));
  register16bit register16bit_8 (.D({16{1'b0}}), .clkin(clk), .we(1'b0), .set(res), .Q(register16bit_8_q));
  assign dataout2 = r17 ? register16bit_1_q : 16'bz;  // Controlled_Buffer controlled_buffer_1
  assign dataout2 = r26 ? register16bit_2_q : 16'bz;  // Controlled_Buffer controlled_buffer_2
  assign dataout2 = r25 ? register16bit_3_q : 16'bz;  // Controlled_Buffer controlled_buffer_3
  assign dataout2 = r24 ? register16bit_4_q : 16'bz;  // Controlled_Buffer controlled_buffer_4
  assign dataout2 = r23 ? register16bit_5_q : 16'bz;  // Controlled_Buffer controlled_buffer_5
  assign dataout2 = r22 ? register16bit_6_q : 16'bz;  // Controlled_Buffer controlled_buffer_6
  assign dataout2 = r21 ? register16bit_7_q : 16'bz;  // Controlled_Buffer controlled_buffer_7
  assign dataout2 = r20 ? register16bit_8_q : 16'bz;  // Controlled_Buffer controlled_buffer_8
  assign dataout1 = r17 ? register16bit_1_q : 16'bz;  // Controlled_Buffer controlled_buffer_9
  assign dataout1 = r16 ? register16bit_2_q : 16'bz;  // Controlled_Buffer controlled_buffer_10
  assign dataout1 = r15 ? register16bit_3_q : 16'bz;  // Controlled_Buffer controlled_buffer_11
  assign dataout1 = r14 ? register16bit_4_q : 16'bz;  // Controlled_Buffer controlled_buffer_12
  assign dataout1 = r13 ? register16bit_5_q : 16'bz;  // Controlled_Buffer controlled_buffer_13
  assign dataout1 = r12 ? register16bit_6_q : 16'bz;  // Controlled_Buffer controlled_buffer_14
  assign dataout1 = r11 ? register16bit_7_q : 16'bz;  // Controlled_Buffer controlled_buffer_15
  assign dataout1 = r10 ? register16bit_8_q : 16'bz;  // Controlled_Buffer controlled_buffer_16
  Decoder #(.select(3)) decoder_2 (
    .out0(r10), .out1(r11), .out2(r12), .out3(r13), .out4(r14), .out5(r15), .out6(r16), .out7(r17),
    .sel(read01));  // open: en
  Decoder #(.select(3)) decoder_3 (
    .out0(r20), .out1(r21), .out2(r22), .out3(r23), .out4(r24), .out5(r25), .out6(r26), .out7(r27),
    .sel(read02));  // open: en

  // Other names for the same wires on the sheet: clktun = clk; rst = res
endmodule

module register16bit (
  input  [15:0] D,
  input  clkin,
  input  we,
  input  set,
  output [15:0] Q
);

  wire clk;

  and and_1 (clk, clkin, we);
  D_Flip_Flop d_ff_1 (.D(D[0]), .clk(clk), .Q(Q[0]));  // open: Qn, preset, reset
  D_Flip_Flop d_ff_2 (.D(D[1]), .clk(clk), .Q(Q[1]));  // open: Qn, preset, reset
  D_Flip_Flop d_ff_3 (.D(D[2]), .clk(clk), .Q(Q[2]), .reset(set));  // open: Qn, preset
  D_Flip_Flop d_ff_4 (.D(D[3]), .clk(clk), .Q(Q[3]), .reset(set));  // open: Qn, preset
  D_Flip_Flop d_ff_5 (.D(D[4]), .clk(clk), .Q(Q[4]), .reset(set));  // open: Qn, preset
  D_Flip_Flop d_ff_6 (.D(D[5]), .clk(clk), .Q(Q[5]), .reset(set));  // open: Qn, preset
  D_Flip_Flop d_ff_7 (.D(D[6]), .clk(clk), .Q(Q[6]), .reset(set));  // open: Qn, preset
  D_Flip_Flop d_ff_8 (.D(D[7]), .clk(clk), .Q(Q[7]), .reset(set));  // open: Qn, preset
  D_Flip_Flop d_ff_9 (.D(D[8]), .clk(clk), .Q(Q[8]), .reset(set));  // open: Qn, preset
  D_Flip_Flop d_ff_10 (.D(D[9]), .clk(clk), .Q(Q[9]), .reset(set));  // open: Qn, preset
  D_Flip_Flop d_ff_11 (.D(D[10]), .clk(clk), .Q(Q[10]), .reset(set));  // open: Qn, preset
  D_Flip_Flop d_ff_12 (.D(D[11]), .clk(clk), .Q(Q[11]), .reset(set));  // open: Qn, preset
  D_Flip_Flop d_ff_13 (.D(D[12]), .clk(clk), .Q(Q[12]), .reset(set));  // open: Qn, preset
  D_Flip_Flop d_ff_14 (.D(D[13]), .clk(clk), .Q(Q[13]), .reset(set));  // open: Qn, preset
  D_Flip_Flop d_ff_15 (.D(D[14]), .clk(clk), .Q(Q[14]), .reset(set));  // open: Qn, preset
  D_Flip_Flop d_ff_16 (.D(D[15]), .clk(clk), .Q(Q[15]), .reset(set));  // open: Qn, preset

  // Other names for the same wires on the sheet: reset = set
endmodule

module ALU (
  input  [15:0] dataIn01,
  input  [15:0] dataIn02,
  input  [1:0] opType,
  output [15:0] out_4
);

  wire [15:0] adder16bit_1_res, adder16bit_2_res, not_1_out, or_1_out;

  assign or_1_out = dataIn01 | dataIn02;  // OR_Gate or_1, 16 bits wide
  assign not_1_out = ~dataIn02;  // NOT_Gate not_1, 16 bits wide
  adder16bit adder16bit_1 (.A(dataIn01), .B(dataIn02), .res(adder16bit_1_res));  // open: Cin, ovf
  adder16bit adder16bit_2 (.A(dataIn01), .B(dataIn02), .res(adder16bit_2_res));  // open: Cin, ovf
  Multiplexer #(.select(2), .width(16), .enable("false")) multiplexer_1 (
    .in0(adder16bit_1_res), .in1(adder16bit_2_res), .in2(or_1_out), .in3(not_1_out), .out(out_4), .sel(opType));
endmodule

module adder16bit (
  input  Cin,
  input  [15:0] A,
  input  [15:0] B,
  output [15:0] res,
  output ovf
);

  wire fouradder_1_cout, fouradder_2_cout, fouradder_3_cout;
  wire [3:0] xorpass_1_valout, xorpass_2_valout, xorpass_3_valout, xorpass_4_valout;

  xorpass xorpass_1 (.valout(xorpass_1_valout), .val(B[3:0]), .sub(Cin));
  xorpass xorpass_2 (.valout(xorpass_2_valout), .val(B[7:4]), .sub(Cin));
  xorpass xorpass_3 (.valout(xorpass_3_valout), .val(B[11:8]), .sub(Cin));
  xorpass xorpass_4 (.valout(xorpass_4_valout), .val(B[15:12]), .sub(Cin));
  fouradder fouradder_1 (.Cin(Cin), .A(A[3:0]), .B(xorpass_1_valout), .Sum(res[3:0]), .Cout(fouradder_1_cout));
  fouradder fouradder_2 (
    .Cin(fouradder_1_cout), .A(A[7:4]), .B(xorpass_2_valout), .Sum(res[7:4]), .Cout(fouradder_2_cout));
  fouradder fouradder_3 (
    .Cin(fouradder_2_cout), .A(A[11:8]), .B(xorpass_3_valout), .Sum(res[11:8]), .Cout(fouradder_3_cout));
  fouroverflow fouroverflow_1 (.Cin(fouradder_3_cout), .A(A[15:12]), .B(xorpass_4_valout), .Sum(res[15:12]), .ovf(ovf));
endmodule

module Fulladder (
  input  Cin,
  input  A,
  input  B,
  output Sum,
  output Cout
);

  wire and_1_out, and_2_out, xor_1_out;

  xor xor_1 (xor_1_out, A, B);
  xor xor_2 (Sum, Cin, xor_1_out);
  and and_1 (and_1_out, xor_1_out, Cin);
  and and_2 (and_2_out, A, B);
  or or_1 (Cout, and_1_out, and_2_out);

  // Other names for the same wires on the sheet: inA = A; inB = B; inCin = Cin
endmodule

module fouradder (
  input  Cin,
  input  [3:0] A,
  input  [3:0] B,
  output [3:0] Sum,
  output Cout
);

  wire fulladder_1_cout, fulladder_2_cout, fulladder_3_cout;

  Fulladder fulladder_1 (.Cin(Cin), .A(A[0]), .B(B[0]), .Sum(Sum[0]), .Cout(fulladder_1_cout));
  Fulladder fulladder_2 (.Cin(fulladder_1_cout), .A(A[1]), .B(B[1]), .Sum(Sum[1]), .Cout(fulladder_2_cout));
  Fulladder fulladder_3 (.Cin(fulladder_2_cout), .A(A[2]), .B(B[2]), .Sum(Sum[2]), .Cout(fulladder_3_cout));
  Fulladder fulladder_4 (.Cin(fulladder_3_cout), .A(A[3]), .B(B[3]), .Sum(Sum[3]), .Cout(Cout));
endmodule

module fouroverflow (
  input  Cin,
  input  [3:0] A,
  input  [3:0] B,
  output [3:0] Sum,
  output ovf
);

  wire fulladder_1_cout, fulladder_2_cout, fulladder_3_cout, fulladder_4_cout;

  Fulladder fulladder_1 (.Cin(Cin), .A(A[0]), .B(B[0]), .Sum(Sum[0]), .Cout(fulladder_1_cout));
  Fulladder fulladder_2 (.Cin(fulladder_1_cout), .A(A[1]), .B(B[1]), .Sum(Sum[1]), .Cout(fulladder_2_cout));
  Fulladder fulladder_3 (.Cin(fulladder_2_cout), .A(A[2]), .B(B[2]), .Sum(Sum[2]), .Cout(fulladder_3_cout));
  Fulladder fulladder_4 (.Cin(fulladder_3_cout), .A(A[3]), .B(B[3]), .Sum(Sum[3]), .Cout(fulladder_4_cout));
  xor xor_1 (ovf, fulladder_3_cout, fulladder_4_cout);
endmodule

module xorpass (
  input  sub,
  input  [3:0] val,
  output [3:0] valout
);

  xor xor_1 (valout[0], sub, val[0]);
  xor xor_2 (valout[1], sub, val[1]);
  xor xor_3 (valout[2], sub, val[2]);
  xor xor_4 (valout[3], sub, val[3]);
endmodule
